# Fritzing sketch Porta (saved by Fritzing 0.9.3b)
circuit board: 8.23146cm x 8.46351cm
breadboards: 1

parts:
  U1 = NodeMCU V1.0
  J2 = Screw terminal - 2 pins [package=THT]
  J3 = Screw terminal - 2 pins [package=THT]
  J4 = Screw terminal - 2 pins [package=THT]
  Q1 = PNP-Transistor [package="TO92 [THT]"]
  J5 = Screw terminal - 2 pins [package=THT]
  J7 = female pin header, 2 pins [form="♀ (female)"]
  U2 = PIC-ICSP [package=molex-1x6]
  J8 = female pin header, 2 pins [form="♀ (female)"]
  J9 = female pin header, 2 pins [form="♀ (female)"]
  J10 = female pin header, 2 pins [form="♀ (female)"]
  S1 = Square Pushbutton

nets (from the pcb view):
  N1: U1.D0, Q1.C, J10.pin1
  N2: U1.D1, U2.PGM
  N3: U1.D2, U2.PGC
  N4: U1.D3, U2.PGD
  N5: U1.D4, U2.GND
  3V3: U1.3V3, J2.pin2, U2.VCC, J8.pin2
  N6: U1.GND, J2.pin1, Q1.E, J5.pin1, U2.VPP, J8.pin1, J9.pin1
  N7: U1.D5, J7.pin1
  N8: U1.D6, J4.pin2
  N9: U1.D7, J3.pin1
  N10: U1.D8, J3.pin2
  N11: U1.Vin, S1.leg0
  N12: J4.pin1, Q1.B, J10.pin2
  N13: J5.pin2, J9.pin2, S1.leg1

custom parts:
  NodeMCU V1.0: ESP8266 based NodeMCU
